# Fritzing sketch circuit (saved by Fritzing 0.9.3b)
breadboards: 1

parts:
  パーツ1 = Arduino Uno (Rev3)
  LED1 = smd LED [color="Infrared (850nm)" package="1206 [SMD]"]
  LED5 = smd LED [color="Red (633nm)" package="0603 [SMD]"]
  S1 = Pushbutton [package=THT]
  S2 = Pushbutton [package=THT]
  R1 = Resistor [tolerance=±5% resistance=100 package=THT]
  R2 = Resistor [tolerance=±5% resistance=100 package=THT]

nets:
  N1: パーツ1.D12/MISO, R1.Pin_0
  N2: パーツ1.D13/SCK, R2.Pin_0
  N3: パーツ1.D2, S1.leg0
  N4: パーツ1.D3_PWM, S2.leg0
  N5: パーツ1.GND, LED1.cathode, LED5.cathode, S1.leg1, S2.leg1
  N6: LED1.anode, R2.Pin_1
  N7: LED5.anode, R1.Pin_1
