# Fritzing sketch circuit_atmega328 (saved by Fritzing 0.9.3b)
breadboards: 1

parts:
  U1 = atmega328 [package=dip]
  VCC1 = Battery
  C1 = Ceramic Capacitor [capacitance=0.1µF package="100 mil [THT, multilayer]"]
  S1 = Pushbutton [package=THT]
  R1 = Resistor [tolerance=±5% resistance=220 package=THT]
  XTAL1 = Crystal [frequency="16 Mhz" package=THT]
  C2 = Ceramic Capacitor [capacitance=10pF voltage=10V part_number=22pF package="100 mil [THT, multilayer]"]
  C3 = Ceramic Capacitor [capacitance=10pF voltage=10V part_number=22pF package="100 mil [THT, multilayer]"]
  S2 = Pushbutton [package=THT]
  S3 = Pushbutton [package=THT]
  R2 = Resistor [tolerance=±5% resistance=220 package=THT]
  R3 = Resistor [tolerance=±5% resistance=220 package=THT]
  LED1 = LED - 5mm [color="Red (633nm)" package="5 mm [THT]"]
  LED2 = LED - 5mm [color="Infrared (850nm)" package="5 mm [THT]"]

nets:
  N1: U1.RESET, C1.1, R1.Pin_1
  N2: U1.D0_(RX), S2.leg0
  N3: U1.D1_(TX), S3.leg0
  N4: U1.VCC, U1.AVCC, VCC1.+, R1.Pin_0
  N5: U1.GND, VCC1.-, S1.leg1, C2.1, C3.1, S2.leg1, S3.leg1, LED1.cathode, LED2.cathode
  N6: U1.XLAT1, XTAL1.pin_1, C3.0
  N7: U1.XLAT2, XTAL1.pin_0, C2.0
  N8: U1.D12, R2.Pin_1
  N9: U1.D13, R3.Pin_1
  N10: C1.0, S1.leg0
  N11: R2.Pin_0, LED1.anode
  N12: R3.Pin_0, LED2.anode
